# Fritzing sketch Esquematico (saved by Fritzing 1.0.0rc)
breadboards: 1

parts:
  Q1 = pnp-Powertransistor [package="TO220 [THT]"]
  Componente1 = Arduino Uno (Rev3)
  R1 = Resistor [tolerance=±1% power=0.25W resistance=10k package=THT]
  J1 = Screw terminal - 2 pins [package=THT]
  J2 = Screw terminal - 2 pins [package=THT]
  LED1 = LEDs [package=led10mm]
  VCC1 = Battery
  TTP223B2 = TTP223B Capacitive Touch Sensor Module [part_number="Touch sensor"]

nets:
  N1: Q1.base, Componente1.D10_PWM/SS
  N2: Q1.collector, J2.pin2, VCC1.-
  N3: Q1.emitter, R1.Pin_1, J1.pin1, LED1.C
  N4: Componente1.D9_PWM, TTP223B2.VCC
  GND: Componente1.GND, TTP223B2.GND
  N5: Componente1.5V, TTP223B2.SIG
  N6: R1.Pin_0, J1.pin2, J2.pin1, LED1.A, VCC1.+

notes:
  12v DC
  10k

custom parts:
  TTP223B Capacitive Touch Sensor Module: The TTP223B capacitive touch sensor module uses the TTP223B IC. The appropriate voltage is approximately 2 to 5.5 volts.
